# Fritzing sketch CO2 Circuit (saved by Fritzing 0.9.3b)
perfboards: 2

parts:
  Pro_Micro1 = SparkFun Pro Micro
  TD-er1 = MH-Z19 CO2 sensor [part_number=MH-Z19]
  Part1 = Adafruit 128x32 Pi OLED [part_number="Adafruit #3527"]
  M1 = TP4056 Module [part_number=HW-107]
  S1 = SPST Switch [package=switch-spst-smd-a]
  J1 = Camdenboss CTB0158-2 [part_number=CTB0158-2 package=THT]
  BAT1 = 18650 battery holder [package=battery-18650-kit]
  U1 = Mini-360 DC-DC Buck converter [package=THT]

nets:
  N1: Pro_Micro1.TX0, TD-er1.RX
  N2: Pro_Micro1.RX1, TD-er1.TX
  GND: Pro_Micro1.GND, TD-er1.GND, Part1.GND, J1.pin2, U1.OUT-
  N3: Pro_Micro1.2, Part1.SDA
  N4: Pro_Micro1.3, Pro_Micro1.4, Part1.SCL
  VCC: Pro_Micro1.VCC, TD-er1.Vin, Part1.+5V, S1.S, J1.pin1
  N5: M1.pin2, U1.IN-
  N6: M1.pin3, BAT1.-
  N7: M1.pin4, BAT1.+
  N8: M1.pin5, U1.IN+
  N9: S1.P, U1.OUT+

custom parts:
  SparkFun Pro Micro: The Pro Micro is similar to the Pro Mini except with an ATmega32U4 on board. The USB transceiver inside the 32U4 allows us to add USB connectivity on-board and do away with bulky external USB interface. Based on: https://github.com/unorthodox-engineers/unorthodox-arduino/blob/master/Unorthodox/fritzing/parts/Pro%20Micro.fzpz
  Adafruit 128x32 Pi OLED: If you're looking for the most compact li'l display for a Raspberry Pi (most likely a Pi Zero) project, this might be just the thing you need! The Adafruit 128x32 PiOLED is your little OLED pal, ready to snap onto any and all Raspberry Pi computers, to give you a little display. The PiOLED comes with a monochrome 128x32 OLED, with sharp white pixels. The OLED uses only the I2C pins so you have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
  TP4056 Module: TP4056 Lithium Battery Charge Management Module Links: TP4056 website
  18650 battery holder: 18650 Battery Holder
  Mini-360 DC-DC Buck converter: Mini-360 DC-DC Buck converter. Tiny buck step down voltage converter, input voltage 4.75 to 23V output 1 to 17V adjustable. Available from ebay and the like.
